# Fritzing sketch Schemas (saved by Fritzing 0.8.7b)
breadboards: 1

parts:
  RHT1 = Humidity and Temperature Sensor RHT03
  R1 = Resistor [tolerance=±5% resistance=220 package=THT]
  Composant1 = Arduino Uno (Rev3) - ICSP

nets:
  N1: RHT1.Vcc, R1.Pin_1
  N2: RHT1.Data-signal, R1.Pin_0, Composant1.D7
  N3: RHT1.GND_2, Composant1.GND
